# Fritzing sketch 01_blink (saved by Fritzing 0.9.3b)
breadboards: 1

parts:
  Adafruit_HUZZAH_ESP8266_Breakout1 = ESP8266 Breakout [part_number=2471]
  S1 = Pushbutton [package="[THT]"]
  R1 = Resistor [tolerance=±5% resistance=220 package="1206 [SMD]"]
  LED4 = LED - 5mm [color="Red (633nm)" package="5 mm [THT]"]

nets:
  N1: Adafruit_HUZZAH_ESP8266_Breakout1.RST, S1.Pin_1, S1.Pin_2
  N2: Adafruit_HUZZAH_ESP8266_Breakout1.EN, Adafruit_HUZZAH_ESP8266_Breakout1.3V3#11
  N3: Adafruit_HUZZAH_ESP8266_Breakout1.#14, R1.Pin_1
  N4: Adafruit_HUZZAH_ESP8266_Breakout1.GND, S1.Pin_3, S1.Pin_4, LED4.cathode

custom parts:
  ESP8266 Breakout: The HUZZAH ESP8266 breakout is what we designed to make working with this chip super easy and a lot of fun. We took a certified module with an onboard antenna, and plenty of pins, and soldered it onto our designed breakout PCBs. We added in: Reset button, User button that can also put the chip into bootloading mode, Red LED you can blink Level shifting on the UART and reset pin 3.3V out, 500mA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
